// Digital circuit TestCircuit.dig as structural Verilog
module TestCircuit (
);

  wire carwash_1_p1, carwash_1_p2, carwash_1_p3, carwash_1_p4, carwash_1_p5, carwash_1_p6, carwash_1_p7,
       carwash_1_p8;

  // CarWash #(.carwcars(2), .carwclock("true")) carwash_1: pin names not known; wires that end beside it: carwash_1_p1, carwash_1_p2, carwash_1_p3, carwash_1_p4, carwash_1_p5, carwash_1_p6, carwash_1_p7, carwash_1_p8
  LED led_1 (.in(carwash_1_p4));
  LED led_2 (.in(carwash_1_p5));
  LED led_3 (.in(carwash_1_p6));
  TestCircuitAutomat testcircuitautomat_1 (
    .a_2(carwash_1_p4), .b(carwash_1_p5), .c(carwash_1_p6), .r(carwash_1_p7), .C_2(carwash_1_p8),
    .A(carwash_1_p2), .F(carwash_1_p1), .S(carwash_1_p3));
endmodule
