// Digital circuit TestCircuitAutomatFehler.dig as structural Verilog
module TestCircuitAutomatFehler (
  input  a_2,
  input  b,
  input  c,
  input  r,
  input  C_2,
  output A,
  output F,
  output S
);

  wire and_1_out, and_2_out, and_3_out, and_4_out, and_5_out, and_6_out, and_7_out, and_8_out, and_9_out,
       and_10_out, and_11_out, and_12_out, and_13_out, and_14_out, and_15_out, and_16_out, and_17_out,
       and_18_out, and_19_out, and_20_out, and_21_out, and_22_out, and_23_out, and_24_out, and_25_out,
       and_26_out, and_27_out, and_28_out, not_1_out, not_2_out, not_3_out, not_4_out, not_5_out, not_6_out,
       not_7_out, or_2_out, or_3_out, or_4_out, Q0_n, Q1_n, Q2_n;

  not not_1 (not_1_out, a_2);
  not not_2 (not_2_out, b);
  not not_3 (not_3_out, c);
  not not_4 (not_4_out, r);
  not not_5 (not_5_out, Q2_n);
  not not_6 (not_6_out, Q1_n);
  not not_7 (not_7_out, Q0_n);
  and and_1 (and_1_out, Q0_n, Q1_n, not_2_out, not_4_out);
  and and_2 (and_2_out, not_7_out, Q2_n, not_4_out);
  and and_3 (and_3_out, not_7_out, Q2_n, b);
  and and_4 (and_4_out, not_7_out, Q2_n, a_2);
  and and_5 (and_5_out, not_7_out, c);
  and and_6 (and_6_out, not_6_out, b, not_4_out);
  and and_7 (and_7_out, not_6_out, not_5_out, b);
  and and_8 (and_8_out, Q1_n, a_2);
  and and_9 (and_9_out, Q2_n, a_2, not_4_out);
  and and_10 (and_10_out, not_5_out, c);
  and and_11 (and_11_out, c, not_4_out);
  and and_12 (and_12_out, Q0_n, not_6_out, not_5_out, not_1_out, not_4_out);
  and and_13 (and_13_out, not_7_out, Q1_n, not_4_out);
  and and_14 (and_14_out, not_7_out, Q2_n, a_2);
  and and_15 (and_15_out, not_7_out, b);
  and and_16 (and_16_out, Q1_n, c);
  and and_17 (and_17_out, Q1_n, a_2);
  and and_18 (and_18_out, not_5_out, c);
  and and_19 (and_19_out, not_5_out, b);
  and and_20 (and_20_out, Q0_n, not_6_out, not_5_out, a_2, not_2_out, not_3_out);
  and and_21 (and_21_out, Q0_n, Q1_n, not_1_out, b, not_3_out);
  and and_22 (and_22_out, Q0_n, Q2_n, b, not_4_out);
  and and_23 (and_23_out, Q0_n, Q2_n, a_2, not_4_out);
  and and_24 (and_24_out, not_6_out, not_5_out, a_2, not_2_out, not_3_out, not_4_out);
  and and_25 (and_25_out, Q1_n, not_5_out, not_1_out, b, not_3_out, not_4_out);
  and and_26 (and_26_out, not_6_out, Q2_n, not_1_out, not_2_out, c, not_4_out);
  and and_27 (and_27_out, not_7_out, not_6_out, not_5_out);
  and and_28 (and_28_out, Q0_n, Q1_n);
  and and_29 (F, Q1_n, not_5_out);
  and and_30 (S, Q1_n, Q2_n);
  or or_1 (A, and_27_out, and_28_out);
  or or_2 (or_2_out, and_1_out, and_2_out, and_3_out, and_4_out, and_5_out, and_6_out, and_7_out, and_8_out, and_9_out, and_10_out, and_11_out);
  or or_3 (or_3_out, and_12_out, and_13_out, and_14_out, and_15_out, and_16_out, and_17_out, and_18_out, and_19_out);
  or or_4 (or_4_out, and_20_out, and_21_out, and_22_out, and_23_out, and_24_out, and_25_out, and_26_out);
  D_FF u_Q2_n (.D(or_2_out), .C(C_2), .Q(Q2_n));  // open: nQ
  D_FF u_Q1_n (.D(or_3_out), .C(C_2), .Q(Q1_n));  // open: nQ
  D_FF u_Q0_n (.D(or_4_out), .C(C_2), .Q(Q0_n));  // open: nQ
  // Probe testAutomat.fsm on {Q2_n, Q1_n, Q0_n}

  // Notes on the sheet:
  //   C_2: Hz: 2
endmodule
